// Logisim project ESF.circ as structural Verilog: 14 circuits, main circuit main
module main (
  output halt,
  output [31:0] _32_63,
  output [31:0] _0_31
);

  wire clock_1_out, decoder_1_out1, decoder_1_out2, decoder_1_out3, decoder_1_out4, decoder_1_out5,
       decoder_1_out6, multiplexer_1_out, selectsignal_1_out_2;
  wire [2:0] counter_1_q;
  wire [4:0] counter_2_q;
  wire [15:0] keyschedule_1__0_15_2, multiplexer_2_out, register_6_q;
  wire [31:0] F__0_31, keyschedule_1__16_47_2, keyschedule_1__48_79_2, multiplexer_3_out, multiplexer_4_out,
       multiplexer_5_out, multiplexer_6_out, ram_1_data, register_1_q, register_2_q, register_3_q,
       register_4_q, register_5_q, register_7_q, register_8_q, register_9_q, register_10_q, shifter_1_out,
       xor_1_out;

  Clock clock_1 (.out(clock_1_out));
  Counter #(.width(3), .max('h6), .ongoal("stay")) counter_1 (
    .Q(counter_1_q), .clk(clock_1_out));  // open: load, D, count, carry, clr
  RAM #(.addrWidth(3), .dataWidth(32)) ram_1 (.addr(counter_1_q), .data(ram_1_data));  // open: sel, clk, ld, clr
  Decoder #(.select(3), .enable("false")) decoder_1 (
    .out1(decoder_1_out1), .out2(decoder_1_out2), .out3(decoder_1_out3), .out4(decoder_1_out4),
    .out5(decoder_1_out5), .out6(decoder_1_out6), .sel(counter_1_q));  // open: out0, out7
  Comparator #(.width(5)) comparator_1 (.a({5{1'b1}}), .b(counter_2_q), .eq(halt));  // open: gt, lt
  Register #(.width(32)) register_1 (.D(ram_1_data), .Q(register_1_q), .clk(decoder_1_out3));  // open: en, clr
  Register #(.width(32)) register_2 (.D(ram_1_data), .Q(register_2_q), .clk(decoder_1_out4));  // open: en, clr
  Register #(.width(32)) register_3 (.D(ram_1_data), .Q(register_3_q), .clk(decoder_1_out5));  // open: en, clr
  Register #(.width(32)) register_4 (.D(ram_1_data), .Q(register_4_q), .clk(decoder_1_out1));  // open: en, clr
  Register #(.width(32)) register_5 (.D(ram_1_data), .Q(register_5_q), .clk(decoder_1_out2));  // open: en, clr
  Multiplexer #(.enable("false")) multiplexer_1 (.in0(clock_1_out), .in1(1'b1), .out(multiplexer_1_out), .sel(halt));
  Counter #(.width(5), .max('h1f), .ongoal("stay")) counter_2 (
    .count(decoder_1_out6), .Q(counter_2_q), .clk(multiplexer_1_out));  // open: load, D, carry, clr
  Register #(.width(16)) register_6 (
    .D(keyschedule_1__0_15_2), .Q(register_6_q), .clk(multiplexer_1_out));  // open: en, clr
  Register #(.width(32)) register_7 (
    .D(keyschedule_1__16_47_2), .Q(register_7_q), .clk(multiplexer_1_out));  // open: en, clr
  Register #(.width(32)) register_8 (
    .D(keyschedule_1__48_79_2), .Q(register_8_q), .clk(multiplexer_1_out));  // open: en, clr
  Register #(.width(32)) register_9 (.D(xor_1_out), .Q(register_9_q), .clk(multiplexer_1_out));  // open: en, clr
  Register #(.width(32)) register_10 (
    .D(multiplexer_5_out), .Q(register_10_q), .clk(multiplexer_1_out));  // open: en, clr
  SelectSignal selectsignal_1 (.in_1(counter_2_q), .out_2(selectsignal_1_out_2));
  Multiplexer #(.width(16), .enable("false")) multiplexer_2 (
    .in0(register_1_q[15:0]), .in1(register_6_q), .out(multiplexer_2_out), .sel(selectsignal_1_out_2));
  Multiplexer #(.width(32), .enable("false")) multiplexer_3 (
    .in0({register_2_q[15:0], register_1_q[31:16]}), .in1(register_7_q), .out(multiplexer_3_out),
    .sel(selectsignal_1_out_2));
  Multiplexer #(.width(32), .enable("false")) multiplexer_4 (
    .in0({register_3_q[15:0], register_2_q[31:16]}), .in1(register_8_q), .out(multiplexer_4_out),
    .sel(selectsignal_1_out_2));
  Multiplexer #(.width(32), .enable("false")) multiplexer_5 (
    .in0(register_4_q), .in1(register_9_q), .out(multiplexer_5_out), .sel(selectsignal_1_out_2));
  Multiplexer #(.width(32), .enable("false")) multiplexer_6 (
    .in0(register_5_q), .in1(register_10_q), .out(multiplexer_6_out), .sel(selectsignal_1_out_2));
  F F (.RoundKey(multiplexer_4_out), .Rightmost_32_bits(multiplexer_5_out), ._0_31(F__0_31));
  Shifter #(.width(32), .shift("rl")) shifter_1 (.in(multiplexer_6_out), .\dist (5'b00111), .out(shifter_1_out));
  KeySchedule keyschedule_1 (
    .RoundCounter(counter_2_q), ._0_15(multiplexer_2_out), ._0_15_2(keyschedule_1__0_15_2),
    ._16_47(multiplexer_3_out), ._16_47_2(keyschedule_1__16_47_2), ._48_79(multiplexer_4_out),
    ._48_79_2(keyschedule_1__48_79_2));
  // Probe on multiplexer_5_out
  // Probe on xor_1_out
  assign xor_1_out = F__0_31 ^ shifter_1_out;  // XOR_Gate xor_1, 32 bits wide
  Multiplexer #(.width(32), .enable("false")) multiplexer_7 (
    .in1(multiplexer_5_out), .out(_0_31), .sel(halt));  // open: in0
  Multiplexer #(.width(32), .enable("false")) multiplexer_8 (.in1(xor_1_out), .out(_32_63), .sel(halt));  // open: in0
endmodule

module S0 (
  input  a,
  input  b,
  input  c,
  input  d,
  output p,
  output q,
  output r,
  output s
);

  wire and_1_out, and_2_out, and_3_out, and_4_out, and_5_out, and_6_out, and_7_out, and_8_out, and_9_out,
       and_10_out, and_11_out, and_12_out, and_13_out, and_14_out, and_15_out, and_16_out, and_17_out,
       and_18_out, and_19_out, and_20_out, not_1_out, not_2_out, not_3_out, not_4_out, not_5_out, not_6_out,
       not_7_out, not_8_out, not_9_out, not_10_out, not_11_out, not_12_out, not_13_out, not_14_out,
       not_15_out, not_16_out, not_17_out, not_18_out, not_19_out, not_20_out, not_21_out, not_22_out,
       not_23_out, not_24_out, not_25_out, not_26_out, not_27_out, not_28_out, not_29_out, not_30_out,
       not_31_out, not_32_out, not_33_out, not_34_out;

  not not_1 (not_1_out, b);
  not not_2 (not_2_out, c);
  not not_3 (not_3_out, a);
  not not_4 (not_4_out, b);
  not not_5 (not_5_out, d);
  not not_6 (not_6_out, a);
  not not_7 (not_7_out, c);
  not not_8 (not_8_out, d);
  not not_9 (not_9_out, b);
  not not_10 (not_10_out, c);
  not not_11 (not_11_out, a);
  not not_12 (not_12_out, d);
  not not_13 (not_13_out, a);
  not not_14 (not_14_out, c);
  not not_15 (not_15_out, b);
  not not_16 (not_16_out, c);
  not not_17 (not_17_out, b);
  not not_18 (not_18_out, d);
  not not_19 (not_19_out, c);
  not not_20 (not_20_out, d);
  not not_21 (not_21_out, a);
  not not_22 (not_22_out, b);
  not not_23 (not_23_out, d);
  not not_24 (not_24_out, c);
  not not_25 (not_25_out, d);
  not not_26 (not_26_out, a);
  not not_27 (not_27_out, b);
  not not_28 (not_28_out, a);
  not not_29 (not_29_out, b);
  not not_30 (not_30_out, d);
  not not_31 (not_31_out, a);
  not not_32 (not_32_out, b);
  not not_33 (not_33_out, c);
  not not_34 (not_34_out, d);
  and and_1 (and_1_out, not_1_out, not_2_out, d);
  and and_2 (and_2_out, not_3_out, not_4_out, c, not_5_out);
  and and_3 (and_3_out, not_6_out, b, not_7_out, not_8_out);
  and and_4 (and_4_out, b, c, d);
  and and_5 (and_5_out, a, not_9_out, not_10_out);
  and and_6 (and_6_out, a, b, c);
  and and_7 (and_7_out, not_11_out, c, not_12_out);
  and and_8 (and_8_out, not_13_out, b, not_14_out, d);
  and and_9 (and_9_out, a, not_15_out, not_16_out);
  and and_10 (and_10_out, a, not_17_out, not_18_out);
  and and_11 (and_11_out, a, not_19_out, not_20_out);
  and and_12 (and_12_out, a, b, c, d);
  and and_13 (and_13_out, not_21_out, not_22_out, not_23_out);
  and and_14 (and_14_out, not_24_out, not_25_out);
  and and_15 (and_15_out, not_26_out, b, d);
  and and_16 (and_16_out, a, not_27_out, c, d);
  and and_17 (and_17_out, not_28_out, not_29_out, not_30_out);
  and and_18 (and_18_out, not_31_out, c);
  and and_19 (and_19_out, a, not_32_out, not_33_out, d);
  and and_20 (and_20_out, a, b, not_34_out);
  or or_1 (p, and_1_out, and_2_out, and_3_out, and_4_out, and_5_out, and_6_out);
  or or_2 (q, and_7_out, and_8_out, and_9_out, and_10_out, and_11_out, and_12_out);
  or or_3 (r, and_13_out, and_14_out, and_15_out, and_16_out);
  or or_4 (s, and_17_out, and_18_out, and_19_out, and_20_out);
endmodule

module S1 (
  input  a,
  input  b,
  input  c,
  input  d,
  output p,
  output q,
  output r,
  output s
);

  wire and_1_out, and_2_out, and_3_out, and_4_out, and_5_out, and_6_out, and_7_out, and_8_out, and_9_out,
       and_10_out, and_11_out, and_12_out, and_13_out, and_14_out, and_15_out, and_16_out, and_17_out,
       and_18_out, and_19_out, and_20_out, and_21_out, not_1_out, not_2_out, not_3_out, not_4_out, not_5_out,
       not_6_out, not_7_out, not_8_out, not_9_out, not_10_out, not_11_out, not_12_out, not_13_out,
       not_14_out, not_15_out, not_16_out, not_17_out, not_18_out, not_19_out, not_20_out, not_21_out,
       not_22_out, not_23_out, not_24_out, not_25_out, not_26_out, not_27_out, not_28_out, not_29_out,
       not_30_out, not_31_out, not_32_out, not_33_out, not_34_out, not_35_out, not_36_out, not_37_out,
       not_38_out;

  not not_1 (not_1_out, a);
  not not_2 (not_2_out, b);
  not not_3 (not_3_out, c);
  not not_4 (not_4_out, a);
  not not_5 (not_5_out, c);
  not not_6 (not_6_out, d);
  not not_7 (not_7_out, a);
  not not_8 (not_8_out, c);
  not not_9 (not_9_out, b);
  not not_10 (not_10_out, a);
  not not_11 (not_11_out, b);
  not not_12 (not_12_out, c);
  not not_13 (not_13_out, a);
  not not_14 (not_14_out, b);
  not not_15 (not_15_out, a);
  not not_16 (not_16_out, d);
  not not_17 (not_17_out, b);
  not not_18 (not_18_out, d);
  not not_19 (not_19_out, c);
  not not_20 (not_20_out, a);
  not not_21 (not_21_out, b);
  not not_22 (not_22_out, d);
  not not_23 (not_23_out, b);
  not not_24 (not_24_out, d);
  not not_25 (not_25_out, a);
  not not_26 (not_26_out, b);
  not not_27 (not_27_out, c);
  not not_28 (not_28_out, d);
  not not_29 (not_29_out, a);
  not not_30 (not_30_out, c);
  not not_31 (not_31_out, d);
  not not_32 (not_32_out, b);
  not not_33 (not_33_out, c);
  not not_34 (not_34_out, d);
  not not_35 (not_35_out, a);
  not not_36 (not_36_out, b);
  not not_37 (not_37_out, d);
  not not_38 (not_38_out, c);
  and and_1 (and_1_out, not_1_out, not_2_out, not_3_out);
  and and_2 (and_2_out, not_4_out, not_5_out, not_6_out);
  and and_3 (and_3_out, not_7_out, b, c, d);
  and and_4 (and_4_out, a, not_8_out, d);
  and and_5 (and_5_out, a, not_9_out, c);
  and and_6 (and_6_out, not_10_out, not_11_out, not_12_out);
  and and_7 (and_7_out, not_13_out, not_14_out, d);
  and and_8 (and_8_out, not_15_out, b, c, not_16_out);
  and and_9 (and_9_out, a, not_17_out, c, not_18_out);
  and and_10 (and_10_out, a, b, not_19_out);
  and and_11 (and_11_out, a, b, d);
  and and_12 (and_12_out, not_20_out, not_21_out, not_22_out);
  and and_13 (and_13_out, not_23_out, c, not_24_out);
  and and_14 (and_14_out, not_25_out, c, d);
  and and_15 (and_15_out, a, not_26_out, not_27_out, d);
  and and_16 (and_16_out, a, b, not_28_out);
  and and_17 (and_17_out, not_29_out, not_30_out, not_31_out);
  and and_18 (and_18_out, not_32_out, not_33_out, not_34_out);
  and and_19 (and_19_out, not_35_out, not_36_out, c, d);
  and and_20 (and_20_out, b, c, not_37_out);
  and and_21 (and_21_out, a, not_38_out, d);
  or or_1 (p, and_1_out, and_2_out, and_3_out, and_4_out, and_5_out);
  or or_2 (q, and_6_out, and_7_out, and_8_out, and_9_out, and_10_out, and_11_out);
  or or_3 (r, and_12_out, and_13_out, and_14_out, and_15_out, and_16_out);
  or or_4 (s, and_17_out, and_18_out, and_19_out, and_20_out, and_21_out);
endmodule

module S2 (
  input  a,
  input  b,
  input  c,
  input  d,
  output p,
  output q,
  output r,
  output s
);

  wire and_1_out, and_2_out, and_3_out, and_4_out, and_5_out, and_6_out, and_7_out, and_8_out, and_9_out,
       and_10_out, and_11_out, and_12_out, and_13_out, and_14_out, and_15_out, and_16_out, and_17_out,
       and_18_out, and_19_out, and_20_out, and_21_out, and_22_out, not_1_out, not_2_out, not_3_out,
       not_4_out, not_5_out, not_6_out, not_7_out, not_8_out, not_9_out, not_10_out, not_11_out, not_12_out,
       not_13_out, not_14_out, not_15_out, not_16_out, not_17_out, not_18_out, not_19_out, not_20_out,
       not_21_out, not_22_out, not_23_out, not_24_out, not_25_out, not_26_out, not_27_out, not_28_out,
       not_29_out, not_30_out, not_31_out, not_32_out, not_33_out, not_34_out, not_35_out;

  not not_1 (not_1_out, b);
  and and_1 (and_1_out, not_1_out, not_2_out, not_3_out);
  not not_2 (not_2_out, c);
  not not_3 (not_3_out, d);
  not not_4 (not_4_out, a);
  and and_2 (and_2_out, not_4_out, c, d);
  and and_3 (and_3_out, b, not_5_out, d);
  not not_5 (not_5_out, c);
  not not_6 (not_6_out, a);
  and and_4 (and_4_out, not_6_out, b, c);
  and and_5 (and_5_out, a, not_7_out, not_8_out);
  not not_7 (not_7_out, b);
  not not_8 (not_8_out, d);
  not not_9 (not_9_out, a);
  not not_10 (not_10_out, c);
  and and_6 (and_6_out, not_9_out, not_10_out, d);
  not not_11 (not_11_out, b);
  and and_7 (and_7_out, not_11_out, c, not_12_out);
  not not_12 (not_12_out, d);
  not not_13 (not_13_out, a);
  and and_8 (and_8_out, not_13_out, b, d);
  and and_9 (and_9_out, a, not_14_out, not_15_out);
  not not_14 (not_14_out, b);
  not not_15 (not_15_out, d);
  and and_10 (and_10_out, a, not_16_out, c);
  not not_16 (not_16_out, b);
  and and_11 (and_11_out, a, c, not_17_out);
  not not_17 (not_17_out, d);
  not not_18 (not_18_out, a);
  not not_19 (not_19_out, b);
  not not_20 (not_20_out, c);
  not not_21 (not_21_out, b);
  not not_22 (not_22_out, d);
  not not_23 (not_23_out, a);
  not not_24 (not_24_out, d);
  not not_25 (not_25_out, a);
  not not_26 (not_26_out, a);
  not not_27 (not_27_out, b);
  not not_28 (not_28_out, a);
  not not_29 (not_29_out, a);
  not not_30 (not_30_out, c);
  not not_31 (not_31_out, d);
  not not_32 (not_32_out, b);
  not not_33 (not_33_out, c);
  not not_34 (not_34_out, c);
  not not_35 (not_35_out, d);
  or or_1 (p, and_1_out, and_2_out, and_3_out, and_4_out, and_5_out);
  and and_12 (and_12_out, not_18_out, not_19_out, not_20_out, d);
  and and_13 (and_13_out, not_21_out, c, not_22_out);
  and and_14 (and_14_out, not_23_out, b, not_24_out);
  and and_15 (and_15_out, not_25_out, b, c);
  and and_16 (and_16_out, a, b, d);
  and and_17 (and_17_out, not_26_out, not_27_out, c);
  and and_18 (and_18_out, not_28_out, c, d);
  and and_19 (and_19_out, not_29_out, b, not_30_out, not_31_out);
  and and_20 (and_20_out, a, not_32_out, not_33_out);
  and and_21 (and_21_out, a, not_34_out, d);
  and and_22 (and_22_out, a, b, c, not_35_out);
  or or_2 (q, and_6_out, and_7_out, and_8_out, and_9_out, and_10_out, and_11_out);
  or or_3 (r, and_12_out, and_13_out, and_14_out, and_15_out, and_16_out);
  or or_4 (s, and_17_out, and_18_out, and_19_out, and_20_out, and_21_out, and_22_out);
endmodule

module S3 (
  input  a,
  input  b,
  input  c,
  input  d,
  output p,
  output q,
  output r,
  output s
);

  wire and_1_out, and_2_out, and_3_out, and_4_out, and_5_out, and_6_out, and_7_out, and_8_out, and_9_out,
       and_10_out, and_11_out, and_12_out, and_13_out, and_14_out, and_15_out, and_16_out, and_17_out,
       and_18_out, and_19_out, and_20_out, and_21_out, not_1_out, not_2_out, not_3_out, not_4_out, not_5_out,
       not_6_out, not_7_out, not_8_out, not_9_out, not_10_out, not_11_out, not_12_out, not_13_out,
       not_14_out, not_15_out, not_16_out, not_17_out, not_18_out, not_19_out, not_20_out, not_21_out,
       not_22_out, not_23_out, not_24_out, not_25_out, not_26_out, not_27_out, not_28_out, not_29_out,
       not_30_out, not_31_out, not_32_out;

  not not_1 (not_1_out, a);
  and and_1 (and_1_out, not_1_out, not_2_out, d);
  not not_2 (not_2_out, b);
  not not_3 (not_3_out, a);
  not not_4 (not_4_out, b);
  and and_2 (and_2_out, not_3_out, not_4_out, c);
  not not_5 (not_5_out, a);
  and and_3 (and_3_out, not_5_out, b, not_6_out);
  not not_6 (not_6_out, c);
  and and_4 (and_4_out, a, not_7_out, not_8_out);
  not not_7 (not_7_out, c);
  not not_8 (not_8_out, d);
  and and_5 (and_5_out, a, b, c, d);
  not not_9 (not_9_out, a);
  not not_10 (not_10_out, b);
  not not_11 (not_11_out, c);
  not not_12 (not_12_out, a);
  not not_13 (not_13_out, d);
  not not_14 (not_14_out, d);
  not not_15 (not_15_out, b);
  not not_16 (not_16_out, c);
  not not_17 (not_17_out, d);
  not not_18 (not_18_out, a);
  not not_19 (not_19_out, b);
  not not_20 (not_20_out, c);
  not not_21 (not_21_out, b);
  not not_22 (not_22_out, d);
  not not_23 (not_23_out, a);
  not not_24 (not_24_out, c);
  not not_25 (not_25_out, c);
  not not_26 (not_26_out, a);
  not not_27 (not_27_out, b);
  not not_28 (not_28_out, d);
  not not_29 (not_29_out, a);
  not not_30 (not_30_out, b);
  not not_31 (not_31_out, c);
  not not_32 (not_32_out, d);
  or or_1 (p, and_1_out, and_2_out, and_3_out, and_4_out, and_5_out);
  and and_6 (and_6_out, not_9_out, not_10_out, not_11_out, d);
  and and_7 (and_7_out, not_12_out, b, not_13_out);
  and and_8 (and_8_out, b, c, not_14_out);
  and and_9 (and_9_out, a, not_15_out, not_16_out, not_17_out);
  and and_10 (and_10_out, a, c, d);
  and and_11 (and_11_out, a, b, d);
  and and_12 (and_12_out, not_18_out, not_19_out, not_20_out, d);
  and and_13 (and_13_out, not_21_out, c, not_22_out);
  and and_14 (and_14_out, not_23_out, b, c);
  and and_15 (and_15_out, a, b, not_24_out);
  and and_16 (and_16_out, a, b, d);
  and and_17 (and_17_out, not_25_out, d);
  and and_18 (and_18_out, not_26_out, not_27_out, c, not_28_out);
  and and_19 (and_19_out, not_29_out, b, d);
  and and_20 (and_20_out, a, not_30_out, not_31_out);
  and and_21 (and_21_out, a, b, c, not_32_out);
  or or_2 (q, and_6_out, and_7_out, and_8_out, and_9_out, and_10_out, and_11_out);
  or or_3 (r, and_12_out, and_13_out, and_14_out, and_15_out, and_16_out);
  or or_4 (s, and_17_out, and_18_out, and_19_out, and_20_out, and_21_out);
endmodule

module S4 (
  input  a,
  input  b,
  input  c,
  input  d,
  output p,
  output q,
  output r,
  output s
);

  wire and_1_out, and_2_out, and_3_out, and_4_out, and_5_out, and_6_out, and_7_out, and_8_out, and_9_out,
       and_10_out, and_11_out, and_12_out, and_13_out, and_14_out, and_15_out, and_16_out, and_17_out,
       and_18_out, and_19_out, and_20_out, and_21_out, and_22_out, not_1_out, not_2_out, not_3_out,
       not_4_out, not_5_out, not_6_out, not_7_out, not_8_out, not_9_out, not_10_out, not_11_out, not_12_out,
       not_13_out, not_14_out, not_15_out, not_16_out, not_17_out, not_18_out, not_19_out, not_20_out,
       not_21_out, not_22_out, not_23_out, not_24_out, not_25_out, not_26_out, not_27_out, not_28_out,
       not_29_out, not_30_out, not_31_out, not_32_out, not_33_out;

  not not_1 (not_1_out, a);
  not not_2 (not_2_out, b);
  not not_3 (not_3_out, c);
  not not_4 (not_4_out, a);
  not not_5 (not_5_out, d);
  not not_6 (not_6_out, c);
  not not_7 (not_7_out, d);
  not not_8 (not_8_out, c);
  not not_9 (not_9_out, b);
  not not_10 (not_10_out, c);
  not not_11 (not_11_out, a);
  not not_12 (not_12_out, c);
  not not_13 (not_13_out, d);
  not not_14 (not_14_out, c);
  not not_15 (not_15_out, d);
  not not_16 (not_16_out, a);
  not not_17 (not_17_out, b);
  not not_18 (not_18_out, b);
  not not_19 (not_19_out, a);
  not not_20 (not_20_out, d);
  not not_21 (not_21_out, b);
  not not_22 (not_22_out, c);
  not not_23 (not_23_out, d);
  not not_24 (not_24_out, c);
  not not_25 (not_25_out, a);
  and and_1 (and_1_out, not_25_out, not_26_out, not_27_out);
  not not_26 (not_26_out, b);
  not not_27 (not_27_out, c);
  not not_28 (not_28_out, a);
  not not_29 (not_29_out, b);
  and and_2 (and_2_out, not_28_out, not_29_out, d);
  not not_30 (not_30_out, b);
  and and_3 (and_3_out, not_30_out, not_31_out, d);
  not not_31 (not_31_out, c);
  and and_4 (and_4_out, b, c, not_32_out);
  not not_32 (not_32_out, d);
  and and_5 (and_5_out, a, b, not_33_out);
  not not_33 (not_33_out, d);
  and and_6 (and_6_out, a, b, c);
  and and_7 (and_7_out, not_1_out, not_2_out, not_3_out, d);
  and and_8 (and_8_out, not_4_out, c, not_5_out);
  and and_9 (and_9_out, b, not_6_out, not_7_out);
  and and_10 (and_10_out, a, c, d);
  and and_11 (and_11_out, a, b, not_8_out);
  and and_12 (and_12_out, not_9_out, not_10_out, d);
  and and_13 (and_13_out, not_11_out, b, not_12_out, not_13_out);
  and and_14 (and_14_out, b, c, d);
  and and_15 (and_15_out, a, not_14_out, d);
  and and_16 (and_16_out, a, c, not_15_out);
  and and_17 (and_17_out, not_16_out, not_17_out, d);
  and and_18 (and_18_out, not_18_out, c, d);
  and and_19 (and_19_out, not_19_out, b, c);
  and and_20 (and_20_out, b, c, not_20_out);
  and and_21 (and_21_out, a, not_21_out, not_22_out, not_23_out);
  and and_22 (and_22_out, a, b, not_24_out, d);
  or or_1 (p, and_7_out, and_8_out, and_9_out, and_10_out, and_11_out);
  or or_2 (q, and_12_out, and_13_out, and_14_out, and_15_out, and_16_out);
  or or_3 (r, and_17_out, and_18_out, and_19_out, and_20_out, and_21_out, and_22_out);
  or or_4 (s, and_1_out, and_2_out, and_3_out, and_4_out, and_5_out, and_6_out);
endmodule

module S5 (
  input  a,
  input  b,
  input  c,
  input  d,
  output p,
  output q,
  output r,
  output s
);

  wire and_1_out, and_2_out, and_3_out, and_4_out, and_5_out, and_6_out, and_7_out, and_8_out, and_9_out,
       and_10_out, and_11_out, and_12_out, and_13_out, and_14_out, and_15_out, and_16_out, and_17_out,
       and_18_out, and_19_out, and_20_out, and_21_out, and_22_out, not_1_out, not_2_out, not_3_out,
       not_4_out, not_5_out, not_6_out, not_7_out, not_8_out, not_9_out, not_10_out, not_11_out, not_12_out,
       not_13_out, not_14_out, not_15_out, not_16_out, not_17_out, not_18_out, not_19_out, not_20_out,
       not_21_out, not_22_out, not_23_out, not_24_out, not_25_out, not_26_out, not_27_out, not_28_out,
       not_29_out, not_30_out, not_31_out, not_32_out, not_33_out, not_34_out, not_35_out, not_36_out;

  not not_1 (not_1_out, a);
  not not_2 (not_2_out, b);
  not not_3 (not_3_out, c);
  not not_4 (not_4_out, d);
  not not_5 (not_5_out, a);
  not not_6 (not_6_out, a);
  not not_7 (not_7_out, a);
  not not_8 (not_8_out, b);
  not not_9 (not_9_out, c);
  not not_10 (not_10_out, d);
  not not_11 (not_11_out, a);
  not not_12 (not_12_out, b);
  not not_13 (not_13_out, c);
  not not_14 (not_14_out, a);
  not not_15 (not_15_out, c);
  not not_16 (not_16_out, d);
  not not_17 (not_17_out, a);
  not not_18 (not_18_out, d);
  not not_19 (not_19_out, c);
  not not_20 (not_20_out, a);
  and and_1 (and_1_out, not_20_out, not_21_out, not_22_out);
  not not_21 (not_21_out, b);
  not not_22 (not_22_out, d);
  not not_23 (not_23_out, a);
  not not_24 (not_24_out, b);
  and and_2 (and_2_out, not_23_out, not_24_out, c);
  not not_25 (not_25_out, c);
  and and_3 (and_3_out, b, not_25_out, d);
  not not_26 (not_26_out, c);
  and and_4 (and_4_out, a, not_26_out, d);
  and and_5 (and_5_out, a, c, not_27_out);
  not not_27 (not_27_out, d);
  not not_28 (not_28_out, a);
  and and_6 (and_6_out, not_28_out, not_29_out, not_30_out);
  not not_29 (not_29_out, b);
  not not_30 (not_30_out, c);
  not not_31 (not_31_out, a);
  not not_32 (not_32_out, b);
  and and_7 (and_7_out, not_31_out, not_32_out, d);
  not not_33 (not_33_out, b);
  not not_34 (not_34_out, c);
  and and_8 (and_8_out, not_33_out, not_34_out, d);
  and and_9 (and_9_out, b, c, not_35_out);
  not not_35 (not_35_out, d);
  and and_10 (and_10_out, a, b, not_36_out);
  not not_36 (not_36_out, d);
  and and_11 (and_11_out, a, b, c);
  and and_12 (and_12_out, not_1_out, not_2_out, not_3_out, not_4_out);
  and and_13 (and_13_out, not_5_out, c, d);
  and and_14 (and_14_out, not_6_out, b, d);
  and and_15 (and_15_out, not_7_out, b, c);
  and and_16 (and_16_out, a, not_8_out, c);
  and and_17 (and_17_out, a, b, not_9_out, not_10_out);
  and and_18 (and_18_out, not_11_out, not_12_out, not_13_out);
  and and_19 (and_19_out, not_14_out, not_15_out, not_16_out);
  and and_20 (and_20_out, not_17_out, b, c, d);
  and and_21 (and_21_out, a, c, not_18_out);
  and and_22 (and_22_out, a, b, not_19_out);
  or or_1 (r, and_1_out, and_2_out, and_3_out, and_4_out, and_5_out);
  or or_2 (p, and_12_out, and_13_out, and_14_out, and_15_out, and_16_out, and_17_out);
  or or_3 (q, and_18_out, and_19_out, and_20_out, and_21_out, and_22_out);
  or or_4 (s, and_6_out, and_7_out, and_8_out, and_9_out, and_10_out, and_11_out);
endmodule

module S6 (
  input  a,
  input  b,
  input  c,
  input  d,
  output p,
  output q,
  output r,
  output s
);

  wire and_1_out, and_2_out, and_3_out, and_4_out, and_5_out, and_6_out, and_7_out, and_8_out, and_9_out,
       and_10_out, and_11_out, and_12_out, and_13_out, and_14_out, and_15_out, and_16_out, and_17_out,
       and_18_out, and_19_out, and_20_out, and_21_out, and_22_out, not_1_out, not_2_out, not_3_out,
       not_4_out, not_5_out, not_6_out, not_7_out, not_8_out, not_9_out, not_10_out, not_11_out, not_12_out,
       not_13_out, not_14_out, not_15_out, not_16_out, not_17_out, not_18_out, not_19_out, not_20_out,
       not_21_out, not_22_out, not_23_out, not_24_out, not_25_out, not_26_out, not_27_out, not_28_out,
       not_29_out, not_30_out, not_31_out, not_32_out, not_33_out, not_34_out, not_35_out, not_36_out,
       not_37_out, not_38_out;

  not not_1 (not_1_out, a);
  not not_2 (not_2_out, b);
  not not_3 (not_3_out, d);
  not not_4 (not_4_out, c);
  not not_5 (not_5_out, d);
  not not_6 (not_6_out, a);
  not not_7 (not_7_out, b);
  not not_8 (not_8_out, c);
  not not_9 (not_9_out, b);
  not not_10 (not_10_out, d);
  not not_11 (not_11_out, a);
  not not_12 (not_12_out, b);
  not not_13 (not_13_out, d);
  not not_14 (not_14_out, a);
  not not_15 (not_15_out, d);
  not not_16 (not_16_out, b);
  not not_17 (not_17_out, a);
  not not_18 (not_18_out, c);
  not not_19 (not_19_out, c);
  not not_20 (not_20_out, d);
  not not_21 (not_21_out, a);
  not not_22 (not_22_out, b);
  not not_23 (not_23_out, c);
  not not_24 (not_24_out, b);
  not not_25 (not_25_out, c);
  not not_26 (not_26_out, d);
  not not_27 (not_27_out, a);
  not not_28 (not_28_out, d);
  not not_29 (not_29_out, b);
  not not_30 (not_30_out, c);
  not not_31 (not_31_out, a);
  not not_32 (not_32_out, b);
  not not_33 (not_33_out, c);
  not not_34 (not_34_out, d);
  not not_35 (not_35_out, a);
  not not_36 (not_36_out, b);
  not not_37 (not_37_out, b);
  not not_38 (not_38_out, c);
  and and_1 (and_1_out, not_1_out, not_2_out, c, not_3_out);
  and and_2 (and_2_out, b, not_4_out, not_5_out);
  and and_3 (and_3_out, not_6_out, b, c, d);
  and and_4 (and_4_out, a, not_7_out, not_8_out);
  and and_5 (and_5_out, a, not_9_out, d);
  and and_6 (and_6_out, a, b, not_10_out);
  and and_7 (and_7_out, not_11_out, not_12_out, not_13_out);
  and and_8 (and_8_out, not_14_out, c, not_15_out);
  and and_9 (and_9_out, not_16_out, c, d);
  and and_10 (and_10_out, not_17_out, b, not_18_out, d);
  and and_11 (and_11_out, a, not_19_out, not_20_out);
  and and_12 (and_12_out, not_21_out, not_22_out, not_23_out);
  and and_13 (and_13_out, not_24_out, not_25_out, not_26_out);
  and and_14 (and_14_out, not_27_out, b, c);
  and and_15 (and_15_out, b, c, not_28_out);
  and and_16 (and_16_out, a, not_29_out, c, d);
  and and_17 (and_17_out, a, b, not_30_out, d);
  and and_18 (and_18_out, not_31_out, not_32_out, not_33_out, not_34_out);
  and and_19 (and_19_out, not_35_out, c, d);
  and and_20 (and_20_out, a, not_36_out, d);
  and and_21 (and_21_out, a, not_37_out, c);
  and and_22 (and_22_out, a, b, not_38_out);
  or or_1 (p, and_1_out, and_2_out, and_3_out, and_4_out, and_5_out, and_6_out);
  or or_2 (q, and_7_out, and_8_out, and_9_out, and_10_out, and_11_out);
  or or_3 (r, and_12_out, and_13_out, and_14_out, and_15_out, and_16_out, and_17_out);
  or or_4 (s, and_18_out, and_19_out, and_20_out, and_21_out, and_22_out);
endmodule

module S7 (
  input  a,
  input  b,
  input  c,
  input  d,
  output p,
  output q,
  output r,
  output s
);

  wire and_1_out, and_2_out, and_3_out, and_4_out, and_5_out, and_6_out, and_7_out, and_8_out, and_9_out,
       and_10_out, and_11_out, and_12_out, and_13_out, and_14_out, and_15_out, and_16_out, and_17_out,
       and_18_out, and_19_out, and_20_out, and_21_out, and_22_out, not_1_out, not_2_out, not_3_out,
       not_4_out, not_5_out, not_6_out, not_7_out, not_8_out, not_9_out, not_10_out, not_11_out, not_12_out,
       not_13_out, not_14_out, not_15_out, not_16_out, not_17_out, not_18_out, not_19_out, not_20_out,
       not_21_out, not_22_out, not_23_out, not_24_out, not_25_out, not_26_out, not_27_out, not_28_out,
       not_29_out, not_30_out, not_31_out, not_32_out, not_33_out, not_34_out, not_35_out, not_36_out,
       not_37_out;

  not not_1 (not_1_out, a);
  not not_2 (not_2_out, c);
  and and_1 (and_1_out, not_1_out, not_2_out, d);
  not not_3 (not_3_out, b);
  and and_2 (and_2_out, not_3_out, c, not_4_out);
  not not_4 (not_4_out, d);
  not not_5 (not_5_out, c);
  and and_3 (and_3_out, b, not_5_out, not_6_out);
  not not_6 (not_6_out, d);
  not not_7 (not_7_out, a);
  and and_4 (and_4_out, not_7_out, b, d);
  not not_8 (not_8_out, b);
  and and_5 (and_5_out, a, not_8_out, c);
  not not_9 (not_9_out, b);
  not not_10 (not_10_out, c);
  not not_11 (not_11_out, b);
  not not_12 (not_12_out, d);
  not not_13 (not_13_out, a);
  not not_14 (not_14_out, c);
  not not_15 (not_15_out, d);
  not not_16 (not_16_out, b);
  not not_17 (not_17_out, c);
  not not_18 (not_18_out, a);
  not not_19 (not_19_out, d);
  not not_20 (not_20_out, a);
  not not_21 (not_21_out, d);
  not not_22 (not_22_out, a);
  not not_23 (not_23_out, b);
  not not_24 (not_24_out, c);
  not not_25 (not_25_out, d);
  not not_26 (not_26_out, a);
  not not_27 (not_27_out, b);
  not not_28 (not_28_out, c);
  not not_29 (not_29_out, a);
  not not_30 (not_30_out, b);
  not not_31 (not_31_out, d);
  not not_32 (not_32_out, b);
  not not_33 (not_33_out, c);
  not not_34 (not_34_out, d);
  not not_35 (not_35_out, a);
  not not_36 (not_36_out, c);
  not not_37 (not_37_out, d);
  or or_1 (p, and_1_out, and_2_out, and_3_out, and_4_out, and_5_out);
  and and_6 (and_6_out, not_9_out, not_10_out, d);
  and and_7 (and_7_out, not_11_out, c, not_12_out);
  and and_8 (and_8_out, not_13_out, b, not_14_out, not_15_out);
  and and_9 (and_9_out, a, not_16_out, not_17_out);
  and and_10 (and_10_out, a, b, c);
  and and_11 (and_11_out, not_18_out, c, not_19_out);
  and and_12 (and_12_out, not_20_out, b, not_21_out);
  and and_13 (and_13_out, not_22_out, b, c);
  and and_14 (and_14_out, a, not_23_out, not_24_out, not_25_out);
  and and_15 (and_15_out, a, c, d);
  and and_16 (and_16_out, a, b, d);
  and and_17 (and_17_out, not_26_out, not_27_out, not_28_out);
  and and_18 (and_18_out, not_29_out, not_30_out, not_31_out);
  and and_19 (and_19_out, not_32_out, not_33_out, not_34_out);
  and and_20 (and_20_out, not_35_out, b, c, d);
  and and_21 (and_21_out, a, b, not_36_out);
  and and_22 (and_22_out, a, b, not_37_out);
  or or_2 (q, and_6_out, and_7_out, and_8_out, and_9_out, and_10_out);
  or or_3 (r, and_11_out, and_12_out, and_13_out, and_14_out, and_15_out, and_16_out);
  or or_4 (s, and_17_out, and_18_out, and_19_out, and_20_out, and_21_out, and_22_out);
endmodule

module S_Box (
  input  [31:0] in_1,
  output [31:0] out_2
);

  S0 s0_1 (.a(in_1[3]), .b(in_1[2]), .c(in_1[1]), .d(in_1[0]), .p(out_2[3]), .q(out_2[2]), .r(out_2[1]), .s(out_2[0]));
  S1 s1_1 (.a(in_1[7]), .b(in_1[6]), .c(in_1[5]), .d(in_1[4]), .p(out_2[7]), .q(out_2[6]), .r(out_2[5]), .s(out_2[4]));
  S2 s2_1 (
    .a(in_1[11]), .b(in_1[10]), .c(in_1[9]), .d(in_1[8]), .p(out_2[11]), .q(out_2[10]), .r(out_2[9]),
    .s(out_2[8]));
  S3 s3_1 (
    .a(in_1[15]), .b(in_1[14]), .c(in_1[13]), .d(in_1[12]), .p(out_2[15]), .q(out_2[14]), .r(out_2[13]),
    .s(out_2[12]));
  S4 s4_1 (
    .a(in_1[19]), .b(in_1[18]), .c(in_1[17]), .d(in_1[16]), .p(out_2[19]), .q(out_2[18]), .r(out_2[17]),
    .s(out_2[16]));
  S5 s5_1 (
    .a(in_1[23]), .b(in_1[22]), .c(in_1[21]), .d(in_1[20]), .p(out_2[23]), .q(out_2[22]), .r(out_2[21]),
    .s(out_2[20]));
  S6 s6_1 (
    .a(in_1[27]), .b(in_1[26]), .c(in_1[25]), .d(in_1[24]), .p(out_2[27]), .q(out_2[26]), .r(out_2[25]),
    .s(out_2[24]));
  S7 s7_1 (
    .a(in_1[31]), .b(in_1[30]), .c(in_1[29]), .d(in_1[28]), .p(out_2[31]), .q(out_2[30]), .r(out_2[29]),
    .s(out_2[28]));
endmodule

module P_Box (
  input  [31:0] in_1,
  output [31:0] out_2
);


  assign out_2 = {in_1[31], in_1[27], in_1[23], in_1[19], in_1[15], in_1[11], in_1[7], in_1[3], in_1[30], in_1[26], in_1[22], in_1[18], in_1[14], in_1[10], in_1[6], in_1[2], in_1[29], in_1[25], in_1[21], in_1[17], in_1[13], in_1[9], in_1[5], in_1[1], in_1[28], in_1[24], in_1[20], in_1[16], in_1[12], in_1[8], in_1[4], in_1[0]};
endmodule

module KeySchedule (
  input  [4:0] RoundCounter,
  input  [15:0] _0_15,
  input  [31:0] _16_47,
  input  [31:0] _48_79,
  output [15:0] _0_15_2,
  output [31:0] _16_47_2,
  output [31:0] _48_79_2
);

  wire [4:0] adder_1_out;

  Adder #(.width(5)) adder_1 (.a(RoundCounter), .b(5'b00001), .out(adder_1_out));  // open: cin, cout
  assign _16_47_2[31:27] = _16_47[18:14] ^ adder_1_out;  // XOR_Gate xor_1, 5 bits wide
  S0 s0_1 (
    .a(_48_79[14]), .b(_48_79[13]), .c(_48_79[12]), .d(_48_79[11]), .p(_48_79_2[27]), .q(_48_79_2[26]),
    .r(_48_79_2[25]), .s(_48_79_2[24]));
  S0 s0_2 (
    .a(_48_79[18]), .b(_48_79[17]), .c(_48_79[16]), .d(_48_79[15]), .p(_48_79_2[31]), .q(_48_79_2[30]),
    .r(_48_79_2[29]), .s(_48_79_2[28]));

  assign _0_15_2 = {_0_15[2:0], _48_79[31:19]};
  assign _16_47_2[26:0] = {_16_47[13:0], _0_15[15:3]};
  assign _48_79_2[23:0] = {_48_79[10:0], _16_47[31:19]};
endmodule

module F (
  input  [31:0] RoundKey,
  input  [31:0] Rightmost_32_bits,
  output [31:0] _0_31
);

  wire [31:0] S_Box_out_2, xor_1_out;

  assign xor_1_out = RoundKey ^ Rightmost_32_bits;  // XOR_Gate xor_1, 32 bits wide
  S_Box S_Box (.in_1(xor_1_out), .out_2(S_Box_out_2));
  P_Box P_Box (.in_1(S_Box_out_2), .out_2(_0_31));
endmodule

module SelectSignal (
  input  [4:0] in_1,
  output out_2
);

  or or_1 (out_2, in_1[0], in_1[1], in_1[2], in_1[3], in_1[4]);
endmodule
