// Logisim project PRESENT.circ as structural Verilog: 7 circuits, main circuit main
module main (
  output halt,
  output [31:0] _32_63,
  output [31:0] _0_31
);

  wire clock_1_out, decoder_1_out1, decoder_1_out2, decoder_1_out3, decoder_1_out4, decoder_1_out5,
       decoder_1_out6, multiplexer_1_out, selectbitsignal_1_out_2;
  wire [2:0] counter_1_q;
  wire [4:0] counter_2_q;
  wire [15:0] key_transform_1_out_7, multiplexer_4_out, register_8_q;
  wire [31:0] addroundkey_1_o__0_31, addroundkey_1_o__32_63, addroundkey_2_o__0_31, addroundkey_2_o__32_63,
       key_transform_1_out_5, key_transform_1_out_6, multiplexer_2_out, multiplexer_3_out, multiplexer_5_out,
       multiplexer_6_out, p_box_1__0_31_2, p_box_1__32_63_2, ram_1_data, register_1_q, register_2_q,
       register_3_q, register_4_q, register_5_q, register_6_q, register_7_q, register_9_q, register_10_q,
       s_box_layer_1_out_3, s_box_layer_1_out_4;

  Clock clock_1 (.out(clock_1_out));
  Counter #(.width(3), .max('h6), .ongoal("stay")) counter_1 (
    .Q(counter_1_q), .clk(clock_1_out));  // open: load, D, count, carry, clr
  RAM #(.addrWidth(3), .dataWidth(32)) ram_1 (.addr(counter_1_q), .data(ram_1_data));  // open: sel, clk, ld, clr
  Decoder #(.select(3), .enable("false")) decoder_1 (
    .out1(decoder_1_out1), .out2(decoder_1_out2), .out3(decoder_1_out3), .out4(decoder_1_out4),
    .out5(decoder_1_out5), .out6(decoder_1_out6), .sel(counter_1_q));  // open: out0, out7
  Comparator #(.width(5)) comparator_1 (.a(5'b11110), .b(counter_2_q), .eq(halt));  // open: gt, lt
  Counter #(.width(5), .max('h1f), .ongoal("stay")) counter_2 (
    .count(decoder_1_out6), .Q(counter_2_q), .clk(multiplexer_1_out));  // open: load, D, carry, clr
  Multiplexer #(.enable("false")) multiplexer_1 (.in0(clock_1_out), .in1(1'b1), .out(multiplexer_1_out), .sel(halt));
  Register #(.width(32)) register_1 (.D(ram_1_data), .Q(register_1_q), .clk(decoder_1_out3));  // open: en, clr
  Register #(.width(32)) register_2 (.D(ram_1_data), .Q(register_2_q), .clk(decoder_1_out4));  // open: en, clr
  Register #(.width(32)) register_3 (.D(ram_1_data), .Q(register_3_q), .clk(decoder_1_out5));  // open: en, clr
  Register #(.width(32)) register_4 (.D(ram_1_data), .Q(register_4_q), .clk(decoder_1_out1));  // open: en, clr
  Register #(.width(32)) register_5 (.D(ram_1_data), .Q(register_5_q), .clk(decoder_1_out2));  // open: en, clr
  AddRoundKey addroundkey_1 (
    .A__0_31(register_1_q), .A__32_63(register_2_q), .B__0_31(register_4_q), .B__32_63(register_5_q),
    .O__0_31(addroundkey_1_o__0_31), .O__32_63(addroundkey_1_o__32_63), .A__64_79(register_3_q[15:0]));
  SelectBitSignal selectbitsignal_1 (.in_1(counter_2_q), .out_2(selectbitsignal_1_out_2));
  Register #(.width(32)) register_6 (
    .D(key_transform_1_out_5), .Q(register_6_q), .clk(multiplexer_1_out));  // open: en, clr
  Register #(.width(32)) register_7 (
    .D(key_transform_1_out_6), .Q(register_7_q), .clk(multiplexer_1_out));  // open: en, clr
  Register #(.width(16)) register_8 (
    .D(key_transform_1_out_7), .Q(register_8_q), .clk(multiplexer_1_out));  // open: en, clr
  Register #(.width(32)) register_9 (
    .D(addroundkey_2_o__0_31), .Q(register_9_q), .clk(multiplexer_1_out));  // open: en, clr
  Register #(.width(32)) register_10 (
    .D(addroundkey_2_o__32_63), .Q(register_10_q), .clk(multiplexer_1_out));  // open: en, clr
  Multiplexer #(.width(32), .enable("false")) multiplexer_2 (
    .in0(register_1_q), .in1(register_6_q), .out(multiplexer_2_out), .sel(selectbitsignal_1_out_2));
  Multiplexer #(.width(32), .enable("false")) multiplexer_3 (
    .in0(register_2_q), .in1(register_7_q), .out(multiplexer_3_out), .sel(selectbitsignal_1_out_2));
  Multiplexer #(.width(16), .enable("false")) multiplexer_4 (
    .in0(register_3_q[15:0]), .in1(register_8_q), .out(multiplexer_4_out), .sel(selectbitsignal_1_out_2));
  S_Box_Layer s_box_layer_1 (
    .in_1(multiplexer_5_out), .in_2(multiplexer_6_out), .out_3(s_box_layer_1_out_3),
    .out_4(s_box_layer_1_out_4));
  Multiplexer #(.width(32), .enable("false")) multiplexer_5 (
    .in0(addroundkey_1_o__0_31), .in1(register_9_q), .out(multiplexer_5_out), .sel(selectbitsignal_1_out_2));
  Multiplexer #(.width(32), .enable("false")) multiplexer_6 (
    .in0(addroundkey_1_o__32_63), .in1(register_10_q), .out(multiplexer_6_out), .sel(selectbitsignal_1_out_2));
  Key_Transform key_transform_1 (
    .RoundCounter(counter_2_q), ._0_31(multiplexer_2_out), ._32_63(multiplexer_3_out),
    ._64_79(multiplexer_4_out), .out_5(key_transform_1_out_5), .out_6(key_transform_1_out_6),
    .out_7(key_transform_1_out_7));
  P_Box p_box_1 (
    ._0_31(s_box_layer_1_out_3), ._32_63(s_box_layer_1_out_4), ._0_31_2(p_box_1__0_31_2),
    ._32_63_2(p_box_1__32_63_2));
  AddRoundKey addroundkey_2 (
    .A__0_31(key_transform_1_out_5), .A__32_63(key_transform_1_out_6), .B__0_31(p_box_1__0_31_2),
    .B__32_63(p_box_1__32_63_2), .O__0_31(addroundkey_2_o__0_31), .O__32_63(addroundkey_2_o__32_63),
    .A__64_79(key_transform_1_out_7));
  Multiplexer #(.width(32), .enable("false")) multiplexer_7 (
    .in1(addroundkey_2_o__32_63), .out(_32_63), .sel(halt));  // open: in0
  Multiplexer #(.width(32), .enable("false")) multiplexer_8 (
    .in1(addroundkey_2_o__0_31), .out(_0_31), .sel(halt));  // open: in0
  // Probe on addroundkey_2_o__0_31
  // Probe on addroundkey_2_o__32_63
endmodule

// P-Box Layer
module P_Box (
  input  [31:0] _0_31,
  input  [31:0] _32_63,
  output [31:0] _0_31_2,
  output [31:0] _32_63_2
);


  assign _0_31_2 = {_32_63[29], _32_63[25], _32_63[21], _32_63[17], _32_63[13], _32_63[9], _32_63[5], _32_63[1], _0_31[29], _0_31[25], _0_31[21], _0_31[17], _0_31[13], _0_31[9], _0_31[5], _0_31[1], _32_63[28], _32_63[24], _32_63[20], _32_63[16], _32_63[12], _32_63[8], _32_63[4], _32_63[0], _0_31[28], _0_31[24], _0_31[20], _0_31[16], _0_31[12], _0_31[8], _0_31[4], _0_31[0]};
  assign _32_63_2 = {_32_63[31], _32_63[27], _32_63[23], _32_63[19], _32_63[15], _32_63[11], _32_63[7], _32_63[3], _0_31[31], _0_31[27], _0_31[23], _0_31[19], _0_31[15], _0_31[11], _0_31[7], _0_31[3], _32_63[30], _32_63[26], _32_63[22], _32_63[18], _32_63[14], _32_63[10], _32_63[6], _32_63[2], _0_31[30], _0_31[26], _0_31[22], _0_31[18], _0_31[14], _0_31[10], _0_31[6], _0_31[2]};
endmodule

module S_Box (
  input  [3:0] in_1,
  output [3:0] out_2
);

  wire and_1_out, and_2_out, and_3_out, and_4_out, and_5_out, and_6_out, and_7_out, and_8_out, and_9_out,
       and_10_out, and_11_out, and_12_out, and_13_out, and_14_out, and_15_out, and_16_out, and_17_out,
       and_18_out, and_19_out, and_20_out, and_21_out, not_1_out, not_2_out, not_3_out, not_4_out, not_5_out,
       not_6_out, not_7_out, not_8_out, not_9_out, not_10_out, not_11_out, not_12_out, not_13_out,
       not_14_out, not_15_out, not_16_out, not_17_out, not_18_out, not_19_out, not_20_out, not_21_out,
       not_22_out, not_23_out, not_24_out, not_25_out, not_26_out, not_27_out, not_28_out, not_29_out,
       not_30_out, not_31_out, not_32_out, not_33_out, not_34_out;

  not not_1 (not_1_out, in_1[3]);
  not not_2 (not_2_out, in_1[1]);
  not not_3 (not_3_out, in_1[0]);
  not not_4 (not_4_out, in_1[3]);
  not not_5 (not_5_out, in_1[3]);
  not not_6 (not_6_out, in_1[2]);
  not not_7 (not_7_out, in_1[2]);
  not not_8 (not_8_out, in_1[3]);
  not not_9 (not_9_out, in_1[2]);
  not not_10 (not_10_out, in_1[1]);
  not not_11 (not_11_out, in_1[2]);
  not not_12 (not_12_out, in_1[1]);
  not not_13 (not_13_out, in_1[2]);
  not not_14 (not_14_out, in_1[0]);
  not not_15 (not_15_out, in_1[3]);
  not not_16 (not_16_out, in_1[1]);
  not not_17 (not_17_out, in_1[3]);
  not not_18 (not_18_out, in_1[2]);
  not not_19 (not_19_out, in_1[3]);
  not not_20 (not_20_out, in_1[0]);
  not not_21 (not_21_out, in_1[2]);
  not not_22 (not_22_out, in_1[1]);
  not not_23 (not_23_out, in_1[2]);
  not not_24 (not_24_out, in_1[0]);
  not not_25 (not_25_out, in_1[3]);
  not not_26 (not_26_out, in_1[2]);
  not not_27 (not_27_out, in_1[3]);
  not not_28 (not_28_out, in_1[3]);
  not not_29 (not_29_out, in_1[1]);
  not not_30 (not_30_out, in_1[0]);
  not not_31 (not_31_out, in_1[2]);
  not not_32 (not_32_out, in_1[0]);
  not not_33 (not_33_out, in_1[0]);
  not not_34 (not_34_out, in_1[1]);
  and and_1 (and_1_out, not_1_out, not_2_out, not_3_out);
  and and_2 (and_2_out, not_4_out, in_1[1], in_1[0]);
  and and_3 (and_3_out, not_5_out, in_1[2], in_1[1]);
  and and_4 (and_4_out, in_1[3], not_6_out, in_1[0]);
  and and_5 (and_5_out, in_1[3], not_7_out, in_1[1]);
  and and_6 (and_6_out, not_8_out, not_9_out, not_10_out);
  and and_7 (and_7_out, not_11_out, not_12_out, in_1[0]);
  and and_8 (and_8_out, not_13_out, in_1[1], not_14_out);
  and and_9 (and_9_out, not_15_out, in_1[2], in_1[1], in_1[0]);
  and and_10 (and_10_out, in_1[3], in_1[2], not_16_out);
  and and_11 (and_11_out, not_17_out, not_18_out, in_1[1]);
  and and_12 (and_12_out, not_19_out, in_1[1], not_20_out);
  and and_13 (and_13_out, in_1[3], not_21_out, not_22_out);
  and and_14 (and_14_out, in_1[3], not_23_out, not_24_out);
  and and_15 (and_15_out, in_1[3], in_1[2], in_1[0]);
  and and_16 (and_16_out, not_25_out, not_26_out, in_1[0]);
  and and_17 (and_17_out, not_27_out, in_1[1], in_1[0]);
  and and_18 (and_18_out, not_28_out, in_1[2], not_29_out, not_30_out);
  and and_19 (and_19_out, in_1[3], not_31_out, not_32_out);
  and and_20 (and_20_out, in_1[3], in_1[1], not_33_out);
  and and_21 (and_21_out, in_1[3], in_1[2], not_34_out, in_1[0]);
  or or_1 (out_2[3], and_1_out, and_2_out, and_3_out, and_4_out, and_5_out);
  or or_2 (out_2[2], and_6_out, and_7_out, and_8_out, and_9_out, and_10_out);
  or or_3 (out_2[1], and_11_out, and_12_out, and_13_out, and_14_out, and_15_out);
  or or_4 (out_2[0], and_16_out, and_17_out, and_18_out, and_19_out, and_20_out, and_21_out);
endmodule

module Key_Transform (
  input  [4:0] RoundCounter,
  input  [31:0] _0_31,
  input  [31:0] _32_63,
  input  [15:0] _64_79,
  output [31:0] out_5,
  output [31:0] out_6,
  output [15:0] out_7
);

  wire [4:0] adder_1_out;

  Adder #(.width(5)) adder_1 (.a(RoundCounter), .b(5'b00001), .out(adder_1_out));  // open: cin, cout
  assign out_5[19:15] = adder_1_out ^ _32_63[6:2];  // XOR_Gate xor_1, 5 bits wide
  S_Box s_box_1 (.in_1(_0_31[18:15]), .out_2(out_7[15:12]));

  assign {out_5[31:20], out_5[14:0]} = {_32_63[18:7], _32_63[1:0], _0_31[31:19]};
  assign out_6 = {_0_31[2:0], _64_79, _32_63[31:19]};
  assign out_7[11:0] = _0_31[14:3];
endmodule

module S_Box_Layer (
  input  [31:0] in_1,
  input  [31:0] in_2,
  output [31:0] out_3,
  output [31:0] out_4
);

  S_Box s_box_1 (.in_1(in_1[3:0]), .out_2(out_3[3:0]));
  S_Box s_box_2 (.in_1(in_1[7:4]), .out_2(out_3[7:4]));
  S_Box s_box_3 (.in_1(in_1[11:8]), .out_2(out_3[11:8]));
  S_Box s_box_4 (.in_1(in_1[15:12]), .out_2(out_3[15:12]));
  S_Box s_box_5 (.in_1(in_1[19:16]), .out_2(out_3[19:16]));
  S_Box s_box_6 (.in_1(in_1[23:20]), .out_2(out_3[23:20]));
  S_Box s_box_7 (.in_1(in_1[27:24]), .out_2(out_3[27:24]));
  S_Box s_box_8 (.in_1(in_1[31:28]), .out_2(out_3[31:28]));
  S_Box s_box_9 (.in_1(in_2[3:0]), .out_2(out_4[3:0]));
  S_Box s_box_10 (.in_1(in_2[7:4]), .out_2(out_4[7:4]));
  S_Box s_box_11 (.in_1(in_2[11:8]), .out_2(out_4[11:8]));
  S_Box s_box_12 (.in_1(in_2[15:12]), .out_2(out_4[15:12]));
  S_Box s_box_13 (.in_1(in_2[19:16]), .out_2(out_4[19:16]));
  S_Box s_box_14 (.in_1(in_2[23:20]), .out_2(out_4[23:20]));
  S_Box s_box_15 (.in_1(in_2[27:24]), .out_2(out_4[27:24]));
  S_Box s_box_16 (.in_1(in_2[31:28]), .out_2(out_4[31:28]));
endmodule

module AddRoundKey (
  input  [31:0] A__0_31,
  input  [31:0] A__32_63,
  input  [15:0] A__64_79,
  input  [31:0] B__0_31,
  input  [31:0] B__32_63,
  output [31:0] O__0_31,
  output [31:0] O__32_63
);

  assign O__0_31 = {A__32_63[15:0], A__0_31[31:16]} ^ B__0_31;  // XOR_Gate xor_1, 32 bits wide
  assign O__32_63 = {A__64_79, A__32_63[31:16]} ^ B__32_63;  // XOR_Gate xor_2, 32 bits wide
endmodule

// Select
module SelectBitSignal (
  input  [4:0] in_1,
  output out_2
);

  or or_1 (out_2, in_1[0], in_1[1], in_1[2], in_1[3], in_1[4]);
endmodule
